# Fritzing sketch Untitled Sketch (saved by Fritzing 0.9.3b)

parts:
  S1 = Round Pushbutton
  S2 = Round Pushbutton
  U1 = RJ45 Jack [package=rj45-8]
  LCM1602_IIC2 = LCM1602 IIC [part_number="LCM1602 IIC" chip_label="LCM1602 IIC" package="DIP (Dual Inline) [THT]"]
  LCD2 = LCD screen  # not connected
  Composant1 = Arduino Pro Micro (Clone)
  J1 = Piezo Speaker

nets:
  GND: S1.leg0, S2.leg0, U1.2, LCM1602_IIC2.GND, Composant1.GND, J1.pin1
  N1: S1.leg1, Composant1.D7
  N2: S2.leg1, Composant1.D8
  VCC: U1.1, LCM1602_IIC2.VCC, Composant1.VCC
  N3: U1.3, Composant1.D16
  N4: U1.4, Composant1.D14
  N5: U1.5, Composant1.D15
  N6: LCM1602_IIC2.SDA, Composant1.D2
  N7: LCM1602_IIC2.SCL, Composant1.D3
  N8: Composant1.D9, J1.pin2

custom parts:
  LCM1602 IIC: I2C-Module to use a 1602 or 2004 LCD on with the wire.h libory Serial LCD Modul
